# Fritzing sketch diagram (saved by Fritzing 0.9.3b)
breadboards: 1

parts:
  Part1 = Arduino Uno (Rev3)
  LCD1 = LCD screen
  R1 = Trimmer Potentiometer [maximum_resistance=10kΩ package=THT]
  RHT1 = Humidity and Temperature Sensor RHT03
  R2 = Resistor [tolerance=±5% resistance=330 package=THT]
  R3 = Resistor [tolerance=±5% resistance=330 package=THT]
  R4 = Resistor [tolerance=±5% resistance=1k package=THT]

nets:
  N1: Part1.D8, RHT1.Data-signal, R4.Pin_1
  GND: Part1.GND, LCD1.VSS, LCD1.R/W, R1.leg1, RHT1.GND_2
  N2: Part1.D2, LCD1.DB7
  N3: Part1.D3_PWM, LCD1.DB6
  N4: Part1.D4, LCD1.DB5
  N5: Part1.D5_PWM, LCD1.DB4
  N6: Part1.D6_PWM, LCD1.E
  N7: Part1.D7, LCD1.RS
  5V: Part1.5V, LCD1.VDD, LCD1.LED-, R1.leg2, RHT1.Vcc, R2.Pin_1, R3.Pin_1, R4.Pin_0
  N8: LCD1.V0, R1.wiper
  N9: LCD1.LED+, R2.Pin_0, R3.Pin_0

// code stored in the sketch: sketch.ino
/* Arduino Weather Station
 * 
 * Sketch for a compact Arduino Weather Station composed of a DHT11 sensor, an LCD display, and (soon) a Wi-Fi module
 * The sensor calculates the actual temperature, heat index (air temperature combined with relative humidity, in shaded areas), but not "feels like"/apparent temperature (heat index stuff, combined with wind speed/wind chill)
 * TODO: next steps are to get the screen to print sensor data... So it is not only displayed on Serial monitor
 */

// include libraries
#include <LiquidCrystal.h>
#include "DHT.h"

// digital pin connected to the DHT sensor
// (note for "Feather HUZZAH ESP8266" board: use pins 3, 4, 5, 12, 13 or 14; pin 15 can work but DHT must be disconnected during program upload): 
// (current board is Arduino UNO so ignore about note above)
#define DHTPIN 8   

// define as whatever type of sensor you're using: DHT11 / DHT21 / DHT22
#define DHTTYPE DHT11   // DHT11 // DHT21: (AM2301) // DHT22: (AM2302, AM2321)

// initialize the library by associating any needed LCD interface pin with the arduino pin number it is connected to
const int rs = 7, en = 6, d4 = 5, d5 = 4, d6 = 3, d7 = 2;
LiquidCrystal lcd(rs, en, d4, d5, d6, d7);

// initialize DHT sensor
// note that older versions of this library took an optional third parameter to tweak the timings for faster processors.
// this parameter is no longer needed as the current DHT reading algorithm adjusts itself to work on faster processors.
DHT dht(DHTPIN, DHTTYPE);

// loop miliseconds count
int dhtMs = 0;   // Delta in miliseconds since last DHT run
const int DHTDELAY = 3000;   // DHT sensor (simulated) delay

void setup() {
  // set up the LCD's number of columns and rows:
  lcd.begin(16, 2);

  // print a message to the LCD.
  lcd.print("hello, worldo!");
	
	// DHT sensor setup code
	Serial.begin(9600);   // Set bps rate for serial communication (for Serial Monitor only, at the moment)
  Serial.println(F("DHT11 test!"));
  dht.begin();
}

// * note that I cannot use delays like in the DHT tester code, I have to make sure both devices (LCD and DHT11) run sequentially without stopping each other, like they were in parallel execution
// * also note that the millis() variable will reset to 0 after some time... But one problem at a time, I will address this later
void loop() {
  // set the cursor to column 0, line 1
  // (note: line 1 is the second row, since counting begins with 0):
  lcd.setCursor(0, 1);

  // print the number of seconds since reset:
  lcd.print(millis() / 1000);

  // DHT code: runs once approximately every DHTDELAY miliseconds because: 
  // reading temperature or humidity takes about 250 milliseconds
  // DHT11 sensor readings may also be up to 2 seconds 'old' (its a very slow sensor)
	if (int(millis() - dhtMs) >= DHTDELAY) {
		// Serial.println("Run DHT! " + String(millis()) + " " + String(dhtMs) + " " + String(dhtMs - int(millis())) + " " + String(DHTDELAY));
		
		float h = dht.readHumidity();
		float t = dht.readTemperature();
		float f = dht.readTemperature(true);
		
		dhtMs = millis(); // placed here so "return" doesn't leave the loop before resetting this variable

		if (isnan(h) || isnan(t) || isnan(f)) {
	    Serial.println(F("Failed to read from DHT sensor!"));
  	  return;
	  }
		
		float hif = dht.computeHeatIndex(f, h);
		float hic = dht.computeHeatIndex(t, h, false);
		
		Serial.print(F("Humidity: "));
	  Serial.print(h);
	  Serial.print(F("%  Temperature: "));
	  Serial.print(t);
	  Serial.print(F("°C "));
	  Serial.print(f);
	  Serial.print(F("°F  Heat index: "));
	  Serial.print(hic);
	  Serial.print(F("°C "));
	  Serial.print(hif);
	  Serial.println(F("°F"));
	}
}
